# Fritzing sketch diagram (saved by Fritzing 0.9.2b)
breadboards: 1

parts:
  Motor_Shield = Arduino Motor Shield (Rev3)
  Motor = Stepper Motor - Bipolar
  Power_12V_2A = Power plug

nets:
  N1: Motor_Shield.B-, Motor.D
  N2: Motor_Shield.B+, Motor.B
  N3: Motor_Shield.A-, Motor.C
  N4: Motor_Shield.A+, Motor.A
  N5: Motor_Shield.VMOT, Power_12V_2A.GND
  VIN: Motor_Shield.VIN, Power_12V_2A.VCC
